// Logisim project CPU.circ as structural Verilog: 1 circuit, main circuit main
module main (
);

  wire CLR_Count, CLR_Reg, JMP_to_Op, K0, K1, K2, K3, L8, L9, OpULA, RegIN, RegTO, S0, S1, S2, S3, S4, S5,
       S6, S7, S8, S9, uc_1_p2, uc_1_p3;
  wire [3:0] HEX0, HEX1, HEX2, HEX3, HEX4, HEX5, R1, R2, R_IN, ula4_1_rgto;
  wire [7:0] BAR_END;

  Hex_Digit_Display hex_digit_display_1 (.value(HEX5));  // open: dp
  LED u_L9 (.in(L9));
  LED u_L8 (.in(L8));
  // DipSwitch #(.NSwitches(1)) S9: pin names not known; wires that end beside it: S9
  // DipSwitch #(.NSwitches(1)) S8: pin names not known; wires that end beside it: S8
  // Digital_Oscilloscope #(.nState(13)) digital_oscilloscope_1: pin names not known; wires that end beside it: S9, BAR_END[0], BAR_END[1], BAR_END[2], BAR_END[3], BAR_END[4], BAR_END[5], BAR_END[6], BAR_END[7], S0
  Hex_Digit_Display hex_digit_display_2 (.value(HEX3));  // open: dp
  Hex_Digit_Display hex_digit_display_3 (.value(HEX4));  // open: dp
  LED L6 (.in(BAR_END[6]));
  LED L5 (.in(BAR_END[5]));
  LED L7 (.in(BAR_END[7]));
  // DipSwitch #(.NSwitches(1)) S5: pin names not known; wires that end beside it: S5
  // DipSwitch #(.NSwitches(1)) S7: pin names not known; wires that end beside it: S7
  // DipSwitch #(.NSwitches(1)) S6: pin names not known; wires that end beside it: S6
  Hex_Digit_Display hex_digit_display_4 (.value(HEX2));  // open: dp
  LED L3 (.in(BAR_END[3]));
  LED L4 (.in(BAR_END[4]));
  // DipSwitch #(.NSwitches(1)) S2: pin names not known; wires that end beside it: S2
  // DipSwitch #(.NSwitches(1)) S3: pin names not known; wires that end beside it: S3
  // DipSwitch #(.NSwitches(1)) S4: pin names not known; wires that end beside it: S4
  Hex_Digit_Display hex_digit_display_5 (.value(HEX0));  // open: dp
  Hex_Digit_Display hex_digit_display_6 (.value(HEX1));  // open: dp
  LED L0 (.in(BAR_END[0]));
  LED L2 (.in(BAR_END[2]));
  LED L1 (.in(BAR_END[1]));
  // DipSwitch #(.NSwitches(1)) S1: pin names not known; wires that end beside it: S1
  // DipSwitch #(.NSwitches(1)) S0: pin names not known; wires that end beside it: S0
  Button u_K3 (.out(K3));
  Button u_K2 (.out(K2));
  Button u_K1 (.out(K1));
  Button u_K0 (.out(K0));
  Count8 count8_1 (
    .CLK(S9), .E(1'b1), .Q0(BAR_END[0]), .Q1(BAR_END[1]), .Q2(BAR_END[2]), .Q3(BAR_END[3]), .Q4(BAR_END[4]),
    .Q5(BAR_END[5]), .Q6(BAR_END[6]), .Q7(BAR_END[7]), .CLR_Master(S0), .JMP_Operando(HEX2), .JMP(JMP_to_Op),
    .CLR(CLR_Count));
  // UC uc_1: pin names not known; wires that end beside it: HEX5[3:2], uc_1_p2, uc_1_p3, HEX5[1:0], HEX4[3:2], uc_1_p2, uc_1_p3, RegTO, OpULA, RegIN, CLR_Reg, CLR_Count, JMP_to_Op
  ULA4 ula4_1 (.RgIN(R_IN), .Operando(HEX2), .RgTO(ula4_1_rgto), .OP(HEX4[1:0]));
  Demultiplexer #(.width(4), .enable("false")) demultiplexer_1 (.out0(R1), .out1(R2), .in(ula4_1_rgto), .sel(RegTO));
  ROM_256x16 rom_256x16_1 (.busAddr8(BAR_END), .busData16({HEX5, HEX4, HEX3, HEX2}), .CLK(S9));
  Reg4 reg4_1 (.Eclock(S9), .D(R1), .Q(HEX1), .CLR(CLR_Reg), .CLR_Master(S0), .ULA(OpULA), .RegTO(HEX5[2]));
  Reg4 reg4_2 (.Eclock(S9), .D(R2), .Q(HEX0), .CLR(CLR_Reg), .CLR_Master(S0), .ULA(OpULA), .RegTO(HEX5[3]));
  Multiplexer #(.width(4), .enable("false")) multiplexer_1 (.in0(HEX1), .in1(HEX0), .out(R_IN), .sel(RegIN));

  // Other names for the same wires on the sheet: ULA[1:0] = HEX4[1:0]; JMP[1:0] = HEX4[3:2]; RgIN[1:0] = HEX5[1:0];
  //   RegTO1 = HEX5[2]; RgTO[1:0] = HEX5[3:2]; RegTO2 = HEX5[3]; L0 = BAR_END[0]; L1 = BAR_END[1]; L2 = BAR_END[2];
  //   L3 = BAR_END[3]; L4 = BAR_END[4]; L5 = BAR_END[5]; L6 = BAR_END[6]; L7 = BAR_END[7]
endmodule
