// Logisim project DE0-CV.circ as structural Verilog: 6 circuits, main circuit CPU
module CPU (
);

  wire CLR_Count, CLR_Reg, JMP_to_Op, K0, K1, K2, K3, L8, L9, OpULA, RegIN, S0, S1, S2, S3, S4, S5, S6, S7,
       S8, S9;
  wire [3:0] HEX0, HEX1, HEX2, HEX3, HEX4, HEX5, R1, R_IN;
  wire [7:0] BAR_END;

  Hex_Digit_Display hex_digit_display_1 (.value(HEX5));  // open: dp
  LED u_L8 (.in(L8));
  LED u_L9 (.in(L9));
  // DipSwitch #(.NSwitches(1)) S9: pin names not known; wires that end beside it: S9
  // DipSwitch #(.NSwitches(1)) S8: pin names not known; wires that end beside it: S8
  // Digital_Oscilloscope #(.nState(13)) digital_oscilloscope_1: pin names not known; wires that end beside it: S9, HEX1[0], HEX1[1], HEX1[2], HEX1[3], HEX0[0], HEX0[1], HEX0[2], HEX0[3], S0
  Hex_Digit_Display hex_digit_display_2 (.value(HEX4));  // open: dp
  Hex_Digit_Display hex_digit_display_3 (.value(HEX3));  // open: dp
  LED L6 (.in(BAR_END[6]));
  LED L7 (.in(BAR_END[7]));
  LED L5 (.in(BAR_END[5]));
  // DipSwitch #(.NSwitches(1)) S6: pin names not known; wires that end beside it: S6
  // DipSwitch #(.NSwitches(1)) S7: pin names not known; wires that end beside it: S7
  // DipSwitch #(.NSwitches(1)) S5: pin names not known; wires that end beside it: S5
  Hex_Digit_Display hex_digit_display_4 (.value(HEX2));  // open: dp
  LED L4 (.in(BAR_END[4]));
  LED L3 (.in(BAR_END[3]));
  // DipSwitch #(.NSwitches(1)) S3: pin names not known; wires that end beside it: S3
  // DipSwitch #(.NSwitches(1)) S2: pin names not known; wires that end beside it: S2
  // DipSwitch #(.NSwitches(1)) S4: pin names not known; wires that end beside it: S4
  Hex_Digit_Display hex_digit_display_5 (.value(HEX0));  // open: dp
  Hex_Digit_Display hex_digit_display_6 (.value(HEX1));  // open: dp
  LED L1 (.in(BAR_END[1]));
  LED L0 (.in(BAR_END[0]));
  LED L2 (.in(BAR_END[2]));
  // DipSwitch #(.NSwitches(1)) S1: pin names not known; wires that end beside it: S1
  // DipSwitch #(.NSwitches(1)) S0: pin names not known; wires that end beside it: S0, HEX4[1:0]
  Button u_K3 (.out(K3));
  Button u_K2 (.out(K2));
  Button u_K0 (.out(K0));
  Button u_K1 (.out(K1));
  Count8 count8_1 (
    .CLK(S9), .E(1'b1), .Q0(BAR_END[0]), .Q1(BAR_END[1]), .Q2(BAR_END[2]), .Q3(BAR_END[3]), .Q4(BAR_END[4]),
    .Q5(BAR_END[5]), .Q6(BAR_END[6]), .Q7(BAR_END[7]), .CLR_Master(S0), .JMP_Operando(HEX2), .JMP(JMP_to_Op),
    .CLR(CLR_Count));
  ULA4 ula4_1 (.RgIN(R_IN), .Operando(HEX2), .RgTO(R1), .OP(HEX4[1:0]));
  UC uc_1 (
    .JMP(HEX4[3:2]), .\Operaçao_de_ULA (OpULA), .Reinicia_Contador(CLR_Count),
    .Reinicia_Registradores(CLR_Reg), .JMP_Para_Operando(JMP_to_Op), .RgIN(HEX5[1:0]), .RegIN(RegIN));
  ROM_256x16 rom_256x16_1 (.busAddr8(BAR_END), .busData16({HEX5, HEX4, HEX3, HEX2}), .CLK(S9), .master_CLR(S0));
  Reg4 reg4_1 (.Eclock(S9), .D(R1), .Q(HEX1), .CLR(CLR_Reg), .CLR_Master(S0), .ULA(OpULA), .RegTO(HEX5[2]));
  Reg4 reg4_2 (.Eclock(S9), .D(R1), .Q(HEX0), .CLR(CLR_Reg), .CLR_Master(S0), .ULA(OpULA), .RegTO(HEX5[3]));
  Multiplexer #(.width(4), .enable("false")) multiplexer_1 (.in0(HEX1), .in1(HEX0), .out(R_IN), .sel(RegIN));

  // Other names for the same wires on the sheet: ULA[1:0] = HEX4[1:0]; JMP[1:0] = HEX4[3:2]; RgIN[1:0] = HEX5[1:0];
  //   RegTO1 = HEX5[2]; RgTO[1:0] = HEX5[3:2]; RegTO2 = HEX5[3]; L0 = BAR_END[0]; L1 = BAR_END[1]; L2 = BAR_END[2];
  //   L3 = BAR_END[3]; L4 = BAR_END[4]; L5 = BAR_END[5]; L6 = BAR_END[6]; L7 = BAR_END[7]; Re5 = HEX0[0];
  //   Re6 = HEX0[1]; Re7 = HEX0[2]; Re8 = HEX0[3]; Re1 = HEX1[0]; Re2 = HEX1[1]; Re3 = HEX1[2]; Re4 = HEX1[3];
  //   R2[3:0] = R1
endmodule

module Count8 (
  input  CLR_Master,
  input  CLR,
  input  CLK,
  input  [3:0] JMP_Operando,
  input  E,
  input  JMP,
  output Q0,
  output Q1,
  output Q2,
  output Q3,
  output Q4,
  output Q5,
  output Q6,
  output Q7
);

  wire _0, _1, _2, _3, and_1_out, and_2_out, and_3_out, and_4_out, and_5_out, and_6_out, and_7_out,
       and_8_out, and_9_out, and_10_out, and_11_out, and_12_out, and_13_out, and_14_out, CLR_t, JMP_t,
       not_1_out, not_2_out, not_3_out, not_4_out, not_5_out, not_6_out, not_7_out, not_8_out, or_2_out,
       or_3_out, or_4_out, or_5_out, or_6_out, or_7_out, or_8_out, or_9_out;

  D_Flip_Flop d_ff_1 (.clk(CLK), .D(JMP), .Q(JMP_t), .reset(CLR_t));  // open: Qn, preset
  or or_1 (CLR_t, CLR_Master, CLR);
  Reg4 reg4_1 (
    .Eclock(CLK), .D(JMP_Operando), .Q({_3, _2, _1, _0}), .CLR(CLR_t), .ULA(1'b1), .RegTO(1'b1));  // open: CLR_Master
  and and_1 (and_1_out, ~_0, JMP_t);  // AND_Gate
  or or_2 (or_2_out, and_1_out, CLR_t);
  not not_1 (not_1_out, CLK);
  and and_2 (and_2_out, JMP_t, _0);
  T_Flip_Flop #(.Pre_Clr_Positions("BELOW_ABOVE")) t_ff_1 (
    .clk(not_1_out), .T(E), .Q(Q0), .preset(and_2_out), .reset(or_2_out));  // open: Qn
  and and_3 (and_3_out, ~_1, JMP_t);  // AND_Gate
  or or_3 (or_3_out, and_3_out, CLR_t);
  T_Flip_Flop #(.Pre_Clr_Positions("BELOW_ABOVE")) t_ff_2 (
    .clk(not_2_out), .T(Q0), .Q(Q1), .preset(and_4_out), .reset(or_3_out));  // open: Qn
  not not_2 (not_2_out, CLK);
  and and_4 (and_4_out, JMP_t, _1);
  not not_3 (not_3_out, CLK);
  and and_5 (and_5_out, Q0, Q1);
  and and_6 (and_6_out, ~_2, JMP_t);  // AND_Gate
  or or_4 (or_4_out, and_6_out, CLR_t);
  T_Flip_Flop #(.Pre_Clr_Positions("BELOW_ABOVE")) t_ff_3 (
    .clk(not_3_out), .T(and_5_out), .Q(Q2), .preset(and_7_out), .reset(or_4_out));  // open: Qn
  and and_7 (and_7_out, JMP_t, _2);
  not not_4 (not_4_out, CLK);
  and and_8 (and_8_out, and_5_out, Q2);
  and and_9 (and_9_out, ~_3, JMP_t);  // AND_Gate
  or or_5 (or_5_out, and_9_out, CLR_t);
  T_Flip_Flop #(.Pre_Clr_Positions("BELOW_ABOVE")) t_ff_4 (
    .clk(not_4_out), .T(and_8_out), .Q(Q3), .preset(and_10_out), .reset(or_5_out));  // open: Qn
  and and_10 (and_10_out, JMP_t, _3);
  not not_5 (not_5_out, CLK);
  and and_11 (and_11_out, and_8_out, Q3);
  or or_6 (or_6_out, JMP_t, CLR_t);
  T_Flip_Flop #(.Pre_Clr_Positions("BELOW_ABOVE")) t_ff_5 (
    .clk(not_5_out), .T(and_11_out), .Q(Q4), .preset(1'b0), .reset(or_6_out));  // open: Qn
  or or_7 (or_7_out, JMP_t, CLR_t);
  not not_6 (not_6_out, CLK);
  and and_12 (and_12_out, and_11_out, Q4);
  T_Flip_Flop #(.Pre_Clr_Positions("BELOW_ABOVE")) t_ff_6 (
    .clk(not_6_out), .T(and_12_out), .Q(Q5), .preset(1'b0), .reset(or_7_out));  // open: Qn
  or or_8 (or_8_out, JMP_t, CLR_t);
  not not_7 (not_7_out, CLK);
  and and_13 (and_13_out, and_12_out, Q5);
  T_Flip_Flop #(.Pre_Clr_Positions("BELOW_ABOVE")) t_ff_7 (
    .clk(not_7_out), .T(and_13_out), .Q(Q6), .preset(1'b0), .reset(or_8_out));  // open: Qn
  and and_14 (and_14_out, and_13_out, Q6);
  or or_9 (or_9_out, JMP_t, CLR_t);
  not not_8 (not_8_out, CLK);
  T_Flip_Flop #(.Pre_Clr_Positions("BELOW_ABOVE")) t_ff_8 (
    .clk(not_8_out), .T(and_14_out), .Q(Q7), .preset(1'b0), .reset(or_9_out));  // open: Qn

  // Other names for the same wires on the sheet: JMP_End[3:0] = {_3, _2, _1, _0}
endmodule

module Reg4 (
  input  CLR,
  input  CLR_Master,
  input  Eclock,
  input  ULA,
  input  RegTO,
  input  [3:0] D,
  output [3:0] Q
);

  wire CLK, CLR_t;

  or or_1 (CLR_t, CLR, CLR_Master);
  and and_1 (CLK, Eclock, ULA, RegTO);
  D_Flip_Flop d_ff_1 (.clk(CLK), .D(D[3]), .Q(Q[3]), .reset(CLR_t));  // open: Qn, preset
  D_Flip_Flop d_ff_2 (.clk(CLK), .D(D[2]), .Q(Q[2]), .reset(CLR_t));  // open: Qn, preset
  D_Flip_Flop d_ff_3 (.clk(CLK), .D(D[1]), .Q(Q[1]), .reset(CLR_t));  // open: Qn, preset
  D_Flip_Flop d_ff_4 (.clk(CLK), .D(D[0]), .Q(Q[0]), .reset(CLR_t));  // open: Qn, preset
endmodule

module UC (
  input  [1:0] RgIN,
  input  [1:0] JMP,
  output RegIN,
  output \Operaçao_de_ULA ,
  output Reinicia_Registradores,
  output Reinicia_Contador,
  output JMP_Para_Operando
);

  wire not_1_out;

  Demultiplexer #(.select(2), .enable("false")) demultiplexer_1 (
    .out0(\Operaçao_de_ULA ), .out1(Reinicia_Registradores), .out2(Reinicia_Contador),
    .out3(JMP_Para_Operando), .in(1'b1), .sel(JMP));
  not not_1 (not_1_out, RgIN[0]);
  and and_1 (RegIN, not_1_out, RgIN[1]);
endmodule

module ROM_256x16 (
  input  [7:0] busAddr8,
  input  CLK,
  input  master_CLR,
  output [15:0] busData16
);

  wire [15:0] ROM_CPU_data;

  ROM #(.dataWidth(16), .Select("high")) ROM_CPU (.addr(busAddr8), .data(ROM_CPU_data));
  Register #(.width(16), .trigger("falling"), .Select("high")) Reg16 (
    .D(ROM_CPU_data), .Q(busData16), .clk(CLK), .clr(master_CLR));  // open: en

  // Notes on the sheet:
  //   contents of ROM_CPU (hex, n*v repeats v):
  //   6004 9102 6201 6305 9002 6002 9003 400 c0d 4*0 9002 6302 6101 9302 6200 6003 800
endmodule

module ULA4 (
  input  [3:0] RgIN,
  input  [3:0] Operando,
  input  [1:0] OP,
  output [3:0] RgTO
);

  wire [3:0] adder_1_out, divider_1_out, multiplier_1_out, subtractor_1_out;

  Adder #(.width(4)) adder_1 (.a(Operando), .b(RgIN), .out(adder_1_out));  // open: cin, cout
  Multiplier #(.width(4)) multiplier_1 (.a(Operando), .b(4'b0010), .out(multiplier_1_out));  // open: cin, cout
  Subtractor #(.width(4)) subtractor_1 (.a(RgIN), .b(Operando), .out(subtractor_1_out));  // open: bin, bout
  Divider #(.width(4)) divider_1 (.a(Operando), .b(4'b0010), .out(divider_1_out));  // open: upper, rem
  Multiplexer #(.select(2), .width(4), .enable("false")) multiplexer_1 (
    .in0(adder_1_out), .in1(multiplier_1_out), .in2(subtractor_1_out), .in3(divider_1_out), .out(RgTO),
    .sel(OP));

  // Other names for the same wires on the sheet: Registrador[3:0] = RgIN
endmodule
