// Logisim project contador.circ as structural Verilog: 2 circuits, main circuit main
module main (
  input  CLK,
  input  E,
  output Q0,
  output Q1,
  output Q2,
  output Q3,
  output Q4,
  output Q5,
  output Q6,
  output Q7
);

  wire and_1_out, and_2_out, and_3_out, and_4_out, and_5_out, and_6_out;

  T_Flip_Flop #(.Pre_Clr_Positions("BELOW_ABOVE")) t_ff_1 (.clk(CLK), .T(E), .Q(Q0));  // open: Qn, preset, reset
  T_Flip_Flop #(.Pre_Clr_Positions("BELOW_ABOVE")) t_ff_2 (.clk(CLK), .T(Q0), .Q(Q1));  // open: Qn, preset, reset
  and and_1 (and_1_out, Q0, Q1);
  T_Flip_Flop #(.Pre_Clr_Positions("BELOW_ABOVE")) t_ff_3 (
    .clk(CLK), .T(and_1_out), .Q(Q2));  // open: Qn, preset, reset
  and and_2 (and_2_out, and_1_out, Q2);
  T_Flip_Flop #(.Pre_Clr_Positions("BELOW_ABOVE")) t_ff_4 (
    .clk(CLK), .T(and_2_out), .Q(Q3));  // open: Qn, preset, reset
  and and_3 (and_3_out, and_2_out, Q3);
  T_Flip_Flop #(.Pre_Clr_Positions("BELOW_ABOVE")) t_ff_5 (
    .clk(CLK), .T(and_3_out), .Q(Q4));  // open: Qn, preset, reset
  and and_4 (and_4_out, and_3_out, Q4);
  T_Flip_Flop #(.Pre_Clr_Positions("BELOW_ABOVE")) t_ff_6 (
    .clk(CLK), .T(and_4_out), .Q(Q5));  // open: Qn, preset, reset
  and and_5 (and_5_out, and_4_out, Q5);
  T_Flip_Flop #(.Pre_Clr_Positions("BELOW_ABOVE")) t_ff_7 (
    .clk(CLK), .T(and_5_out), .Q(Q6));  // open: Qn, preset, reset
  and and_6 (and_6_out, and_5_out, Q6);
  T_Flip_Flop #(.Pre_Clr_Positions("BELOW_ABOVE")) t_ff_8 (
    .clk(CLK), .T(and_6_out), .Q(Q7));  // open: Qn, preset, reset
endmodule

module teste (
);

  wire clock_1_out, main_1_q0, main_1_q1, main_1_q2, main_1_q3, main_1_q4, main_1_q5, main_1_q6, main_1_q7;

  Clock clock_1 (.out(clock_1_out));
  main main_1 (
    .CLK(clock_1_out), .E(1'b1), .Q0(main_1_q0), .Q1(main_1_q1), .Q2(main_1_q2), .Q3(main_1_q3),
    .Q4(main_1_q4), .Q5(main_1_q5), .Q6(main_1_q6), .Q7(main_1_q7));
  LED led_1 (.in(main_1_q0));
  LED led_2 (.in(main_1_q2));
  LED led_3 (.in(main_1_q1));
  LED led_4 (.in(main_1_q4));
  LED led_5 (.in(main_1_q3));
  LED led_6 (.in(main_1_q7));
  LED led_7 (.in(main_1_q6));
  LED led_8 (.in(main_1_q5));
endmodule
