// Logisim project biblioteca.circ as structural Verilog
module Count8 (
  input  CLR_Master,
  input  CLR,
  input  CLK,
  input  [3:0] JMP_Operando,
  input  E,
  input  JMP,
  output Q0,
  output Q1,
  output Q2,
  output Q3,
  output Q4,
  output Q5,
  output Q6,
  output Q7
);

  wire _0, _1, _2, _3, and_1_out, and_2_out, and_3_out, and_4_out, and_5_out, and_6_out, and_7_out,
       and_8_out, and_9_out, and_10_out, and_11_out, and_12_out, and_13_out, and_14_out, CLR_t, JMP_t,
       not_1_out, not_2_out, not_3_out, not_4_out, not_5_out, not_6_out, not_7_out, not_8_out, or_2_out,
       or_3_out, or_4_out, or_5_out, or_6_out, or_7_out, or_8_out, or_9_out;

  D_Flip_Flop d_ff_1 (.clk(CLK), .D(JMP), .Q(JMP_t), .reset(CLR_t));  // open: Qn, preset
  or or_1 (CLR_t, CLR_Master, CLR);
  // Reg4 reg4_1: pin names not known; wires that end beside it: JMP_Operando, CLK, CLR_t, {_3, _2, _1, _0}
  or or_2 (or_2_out, ~JMP_t, _0);  // OR_Gate
  and and_1 (and_1_out, or_2_out, CLR_t);
  not not_1 (not_1_out, CLK);
  and and_2 (and_2_out, JMP_t, _0);
  T_Flip_Flop #(.Pre_Clr_Positions("BELOW_ABOVE")) t_ff_1 (
    .clk(not_1_out), .T(E), .Q(Q0), .preset(and_2_out), .reset(and_1_out));  // open: Qn
  or or_3 (or_3_out, ~JMP_t, _1);  // OR_Gate
  and and_3 (and_3_out, or_3_out, CLR_t);
  not not_2 (not_2_out, CLK);
  T_Flip_Flop #(.Pre_Clr_Positions("BELOW_ABOVE")) t_ff_2 (
    .clk(not_2_out), .T(Q0), .Q(Q1), .preset(and_4_out), .reset(and_3_out));  // open: Qn
  and and_4 (and_4_out, JMP_t, _1);
  not not_3 (not_3_out, CLK);
  and and_5 (and_5_out, Q0, Q1);
  or or_4 (or_4_out, ~JMP_t, _2);  // OR_Gate
  and and_6 (and_6_out, or_4_out, CLR_t);
  T_Flip_Flop #(.Pre_Clr_Positions("BELOW_ABOVE")) t_ff_3 (
    .clk(not_3_out), .T(and_5_out), .Q(Q2), .preset(and_7_out), .reset(and_6_out));  // open: Qn
  and and_7 (and_7_out, JMP_t, _2);
  not not_4 (not_4_out, CLK);
  and and_8 (and_8_out, and_5_out, Q2);
  or or_5 (or_5_out, ~JMP_t, _3);  // OR_Gate
  and and_9 (and_9_out, or_5_out, CLR_t);
  T_Flip_Flop #(.Pre_Clr_Positions("BELOW_ABOVE")) t_ff_4 (
    .clk(not_4_out), .T(and_8_out), .Q(Q3), .preset(and_10_out), .reset(and_9_out));  // open: Qn
  and and_10 (and_10_out, JMP_t, _3);
  not not_5 (not_5_out, CLK);
  and and_11 (and_11_out, and_8_out, Q3);
  or or_6 (or_6_out, JMP_t, CLR_t);
  T_Flip_Flop #(.Pre_Clr_Positions("BELOW_ABOVE")) t_ff_5 (
    .clk(not_5_out), .T(and_11_out), .Q(Q4), .preset(1'b0), .reset(or_6_out));  // open: Qn
  or or_7 (or_7_out, JMP_t, CLR_t);
  not not_6 (not_6_out, CLK);
  and and_12 (and_12_out, and_11_out, Q4);
  T_Flip_Flop #(.Pre_Clr_Positions("BELOW_ABOVE")) t_ff_6 (
    .clk(not_6_out), .T(and_12_out), .Q(Q5), .preset(1'b0), .reset(or_7_out));  // open: Qn
  or or_8 (or_8_out, JMP_t, CLR_t);
  not not_7 (not_7_out, CLK);
  and and_13 (and_13_out, and_12_out, Q5);
  T_Flip_Flop #(.Pre_Clr_Positions("BELOW_ABOVE")) t_ff_7 (
    .clk(not_7_out), .T(and_13_out), .Q(Q6), .preset(1'b0), .reset(or_8_out));  // open: Qn
  and and_14 (and_14_out, and_13_out, Q6);
  or or_9 (or_9_out, JMP_t, CLR_t);
  T_Flip_Flop #(.Pre_Clr_Positions("BELOW_ABOVE")) t_ff_8 (
    .clk(not_8_out), .T(and_14_out), .Q(Q7), .preset(1'b0), .reset(or_9_out));  // open: Qn
  not not_8 (not_8_out, CLK);

  // Other names for the same wires on the sheet: JMP_End[3:0] = {_3, _2, _1, _0}
endmodule

module Reg4 (
  input  CLR,
  input  CLR_Master,
  input  Eclock,
  input  ULA,
  input  RegTO,
  input  [3:0] D,
  output [3:0] Q
);

  wire CLK, CLR_t;

  or or_1 (CLR_t, CLR, CLR_Master);
  and and_1 (CLK, Eclock, ULA, RegTO);
  D_Flip_Flop d_ff_1 (.clk(CLK), .D(D[3]), .Q(Q[3]), .reset(CLR_t));  // open: Qn, preset
  D_Flip_Flop d_ff_2 (.clk(CLK), .D(D[2]), .Q(Q[2]), .reset(CLR_t));  // open: Qn, preset
  D_Flip_Flop d_ff_3 (.clk(CLK), .D(D[1]), .Q(Q[1]), .reset(CLR_t));  // open: Qn, preset
  D_Flip_Flop d_ff_4 (.clk(CLK), .D(D[0]), .Q(Q[0]), .reset(CLR_t));  // open: Qn, preset
endmodule

module UC (
  input  [1:0] RgTO,
  input  [1:0] RgIN,
  input  [1:0] JMP,
  output RegTO,
  output RegIN,
  output \Operaçao_de_ULA ,
  output Reinicia_Registradores,
  output Reinicia_Contador,
  output JMP_Para_Operando
);

  wire not_1_out, not_2_out;

  Demultiplexer #(.select(2), .enable("false")) demultiplexer_1 (
    .out0(\Operaçao_de_ULA ), .out1(Reinicia_Registradores), .out2(Reinicia_Contador),
    .out3(JMP_Para_Operando), .in(1'b1), .sel(JMP));
  not not_1 (not_1_out, RgTO[0]);
  and and_1 (RegTO, not_1_out, RgTO[1]);
  not not_2 (not_2_out, RgIN[0]);
  and and_2 (RegIN, not_2_out, RgIN[1]);
endmodule

module ROM_256x16 (
  input  [7:0] busAddr8,
  input  CLK,
  output [15:0] busData16
);

  wire [15:0] ROM_CPU_data;

  ROM #(.dataWidth(16), .Select("low")) ROM_CPU (.addr(busAddr8), .data(ROM_CPU_data));
  Register #(.width(16), .trigger("falling"), .Select("high")) Reg16 (
    .D(ROM_CPU_data), .Q(busData16), .clk(CLK));  // open: en, clr

  // Notes on the sheet:
  //   contents of ROM_CPU (hex, n*v repeats v):
  //   6005 9101 6202 6304 c08 400 6001 9001 9002 6302 6102 9302 6200 6001 800 6200 6001 800
endmodule

module ULA4 (
  input  [3:0] RgIN,
  input  [3:0] Operando,
  input  [1:0] OP,
  output [3:0] RgTO
);

  wire [3:0] adder_1_out, divider_1_out, multiplier_1_out, subtractor_1_out;

  Adder #(.width(4)) adder_1 (.a(Operando), .b(RgIN), .out(adder_1_out));  // open: cin, cout
  Multiplier #(.width(4)) multiplier_1 (.a(Operando), .b(4'b0010), .out(multiplier_1_out));  // open: cin, cout
  Subtractor #(.width(4)) subtractor_1 (.a(RgIN), .b(Operando), .out(subtractor_1_out));  // open: bin, bout
  Divider #(.width(4)) divider_1 (.a(Operando), .b(4'b0010), .out(divider_1_out));  // open: upper, rem
  Multiplexer #(.select(2), .width(4), .enable("false")) multiplexer_1 (
    .in0(adder_1_out), .in1(multiplier_1_out), .in2(subtractor_1_out), .in3(divider_1_out), .out(RgTO),
    .sel(OP));

  // Other names for the same wires on the sheet: Registrador[3:0] = RgIN
endmodule
