// Logisim project registrador.circ as structural Verilog: 2 circuits, main circuit main
module main (
  input  Eclock,
  input  D1,
  input  D2,
  input  D3,
  input  D4,
  output Q1,
  output Q2,
  output Q3,
  output Q4
);

  D_Flip_Flop d_ff_1 (.clk(Eclock), .D(D1), .Q(Q1));  // open: Qn, preset, reset
  D_Flip_Flop d_ff_2 (.clk(Eclock), .D(D2), .Q(Q2));  // open: Qn, preset, reset
  D_Flip_Flop d_ff_3 (.clk(Eclock), .D(D3), .Q(Q3));  // open: Qn, preset, reset
  D_Flip_Flop d_ff_4 (.clk(Eclock), .D(D4), .Q(Q4));  // open: Qn, preset, reset
endmodule

module teste (
);

  wire clock_1_out, dipswitch_1_p1, dipswitch_1_p2, dipswitch_1_p3, dipswitch_1_p4, main_1_p6, main_1_p7,
       main_1_p8, main_1_p9;

  Clock clock_1 (.out(clock_1_out));
  // DipSwitch dipswitch_1: pin names not known; wires that end beside it: dipswitch_1_p1, dipswitch_1_p2, dipswitch_1_p3, dipswitch_1_p4, clock_1_out, dipswitch_1_p1
  // main main_1: pin names not known; wires that end beside it: clock_1_out, dipswitch_1_p1, dipswitch_1_p2, dipswitch_1_p3, dipswitch_1_p4, main_1_p6, main_1_p7, main_1_p8, main_1_p9
  LED led_1 (.in(main_1_p6));
  LED led_2 (.in(main_1_p7));
  LED led_3 (.in(main_1_p8));
  LED led_4 (.in(main_1_p9));
endmodule
